# Fritzing sketch Oscilloscope (saved by Fritzing 0.9.3b)
breadboards: 1

parts:
  R1 = Resistor [tolerance=±5% resistance=10k package=THT]
  R2 = Resistor [tolerance=±5% resistance=100k package=THT]
  Analog_in = female pin header, 1 pin [form="♀ (female)"]  # not connected
  U2 = LM 358 Dual Op-Amp [package="DIP8 [THT]"]
  R3 = Resistor [tolerance=±5% resistance=22k package=THT]
  R4 = Resistor [tolerance=±5% resistance=4.7k package=THT]
  R5 = Resistor [tolerance=±5% resistance=1k package=THT]
  R6 = Resistor [tolerance=±5% resistance=10k package=THT]
  M0_A4 = female pin header, 1 pin [form="♀ (female)"]
  M0_A1 = female pin header, 1 pin [form="♀ (female)"]
  R7 = Resistor [tolerance=±5% resistance=22k package=THT]
  R8 = Resistor [tolerance=±5% resistance=100k package=THT]
  R9 = Resistor [tolerance=±5% resistance=10k package=THT]
  R10 = Resistor [tolerance=±5% resistance=220 package=THT]
  C1 = Electrolytic Capacitor [capacitance=470µF package="100 mil [THT, electrolytic]"]
  R11 = Resistor [tolerance=±5% resistance=47 package=THT]
  C2 = Electrolytic Capacitor [capacitance=470µF package="100 mil [THT, electrolytic]"]
  M0_5 = female pin header, 1 pin [form="♀ (female)"]  # not connected
  D2 = Schottky Diode [part_number=1N5817 package="300 mil [THT]"]
  D1 = Schottky Diode [part_number=1N5817 package="300 mil [THT]"]
  R12 = Resistor [tolerance=±5% resistance=10k package=THT]
  U1 = LM 358 Dual Op-Amp [package="DIP8 [THT]"]
  R13 = Resistor [tolerance=±5% resistance=0 package=THT]  # not connected

nets:
  N1: R1.Pin_0, R2.Pin_1, U1.connector1
  N2: R1.Pin_1, R3.Pin_0, R12.Pin_0, U1.connector0
  N3: U2.connector0, R6.Pin_1, M0_A4.pin1
  N4: U2.connector1, R3.Pin_1, R6.Pin_0
  N5: U2.connector2, R5.Pin_0
  N6: U2.connector4, R9.Pin_1
  N7: U2.connector5, R7.Pin_1, R8.Pin_0
  N8: U2.connector6, M0_A1.pin1, R8.Pin_1
  3.3V: R4.Pin_0, R9.Pin_0
  N9: R7.Pin_0, R12.Pin_1
  GND: R10.Pin_1, C2.+, U1.connector2, U1.connector4
  N10: C1.-, D2.cathode, D1.anode
  N11: C1.+, R11.Pin_1
  -3.3V: C2.-, U1.connector3
  N12: U1.connector5, U1.connector6

notes:
  [Feather M0 Oscilloscope
  Analog circuit]
